// Logisim project mips_datapath.circ as structural Verilog: 7 circuits, main circuit main
module main (
);

  wire alu_1_zero, and_1_out, clock_1_out, control_1_alusrc, control_1_branch, control_1_jump,
       control_1_memread, control_1_memtoreg, control_1_memwrite, control_1_regdst, control_1_regwrite;
  wire [1:0] control_1_aluop;
  wire [3:0] adder_1_out_2, alucontrol_1_alu_control;
  wire [4:0] multiplexer_1_out;
  wire [27:0] adder_1_out;
  wire [31:0] adder_2_out, alu_1_result, bit_extender_1_out, datamemory_1_readdata,
       instructionmemory_1_instruction, multiplexer_2_out, multiplexer_3_out, multiplexer_4_out,
       multiplexer_5_out, PC_q, registerfile_1_readdata1, registerfile_1_readdata2, shifter_1_out;

  Clock clock_1 (.out(clock_1_out));
  Register #(.width(32)) PC (.D(multiplexer_4_out), .clk(clock_1_out), .Q(PC_q));  // open: en, clr
  Adder #(.width(32)) adder_1 (.a(32'h1), .b(PC_q), .out({adder_1_out_2, adder_1_out}));  // open: cin, cout
  InstructionMemory instructionmemory_1 (.Address(PC_q), .Instruction(instructionmemory_1_instruction));
  Multiplexer #(.width(5)) multiplexer_1 (
    .in0(instructionmemory_1_instruction[20:16]), .in1(instructionmemory_1_instruction[15:11]),
    .out(multiplexer_1_out), .sel(control_1_regdst));
  Control control_1 (
    .Opcode(instructionmemory_1_instruction[31:26]), .RegDst(control_1_regdst), .ALUSrc(control_1_alusrc),
    .MemToReg(control_1_memtoreg), .RegWrite(control_1_regwrite), .MemRead(control_1_memread),
    .MemWrite(control_1_memwrite), .Branch(control_1_branch), .Jump(control_1_jump), .ALUOp(control_1_aluop));
  assign bit_extender_1_out = {{16{instructionmemory_1_instruction[15]}}, instructionmemory_1_instruction[15:0]};  // Bit_Extender bit_extender_1
  RegisterFile registerfile_1 (
    .ReadReg1(instructionmemory_1_instruction[25:21]), .WriteData(multiplexer_5_out),
    .RegWrite(control_1_regwrite), .WriteReg(multiplexer_1_out),
    .ReadReg2(instructionmemory_1_instruction[20:16]), .CLK(clock_1_out),
    .ReadData1(registerfile_1_readdata1), .ReadData2(registerfile_1_readdata2));
  Multiplexer #(.width(32)) multiplexer_2 (
    .in0(registerfile_1_readdata2), .in1(bit_extender_1_out), .out(multiplexer_2_out), .sel(control_1_alusrc));
  Shifter #(.width(32)) shifter_1 (.in(bit_extender_1_out), .\dist (5'b00010), .out(shifter_1_out));
  ALUControl alucontrol_1 (
    .ALUOp(control_1_aluop), .Funct(instructionmemory_1_instruction[5:0]),
    .ALU_Control(alucontrol_1_alu_control));
  Multiplexer #(.width(32)) multiplexer_3 (
    .in0({adder_1_out_2, adder_1_out}), .in1(adder_2_out), .out(multiplexer_3_out), .sel(and_1_out));
  Adder #(.width(32)) adder_2 (
    .a({adder_1_out_2, adder_1_out}), .b(shifter_1_out), .out(adder_2_out));  // open: cin, cout
  and and_1 (and_1_out, control_1_branch, alu_1_zero);
  Multiplexer #(.width(32)) multiplexer_4 (
    .in0(multiplexer_3_out), .in1({adder_1_out_2, instructionmemory_1_instruction[25:0], 2'b00}),
    .out(multiplexer_4_out), .sel(control_1_jump));
  ALU alu_1 (
    .A(registerfile_1_readdata1), .B(multiplexer_2_out), .ALUControl(alucontrol_1_alu_control),
    .Zero(alu_1_zero), .Result(alu_1_result));
  DataMemory datamemory_1 (
    .Address(alu_1_result), .CLK(clock_1_out), .WriteData(registerfile_1_readdata2),
    .MemWrite(control_1_memwrite), .MemRead(control_1_memread), .ReadData(datamemory_1_readdata));
  Multiplexer #(.width(32)) multiplexer_5 (
    .in0(alu_1_result), .in1(datamemory_1_readdata), .out(multiplexer_5_out), .sel(control_1_memtoreg));

  // Notes on the sheet:
  //   Lo puse en 1 para que ande
  //   Pero es PC + 4
  //   PC + 4[31:28]
  //   rd
  //   immediate
  //   26 bits de address
  //   rs
  //   rt
  //   Jump address
  //   PC + 4
endmodule

module InstructionMemory (
  input  [31:0] Address,
  output [31:0] Instruction
);

  ROM #(.addrWidth(24), .dataWidth(32)) rom_1 (.addr(Address[23:0]), .data(Instruction));

  // Notes on the sheet:
  //   contents of rom_1 (hex, n*v repeats v):
  //   853020 ffffffff c dfdfdfdf 34343434
endmodule

module RegisterFile (
  input  [4:0] ReadReg1,
  input  [31:0] WriteData,
  input  RegWrite,
  input  [4:0] WriteReg,
  input  [4:0] ReadReg2,
  input  CLK,
  output [31:0] ReadData1,
  output [31:0] ReadData2
);

  wire demultiplexer_1_out0, demultiplexer_1_out1, demultiplexer_1_out2, demultiplexer_1_out3,
       demultiplexer_1_out4, demultiplexer_1_out5, demultiplexer_1_out6, demultiplexer_1_out7,
       demultiplexer_1_out8, demultiplexer_1_out9, demultiplexer_1_out10, demultiplexer_1_out11,
       demultiplexer_1_out12, demultiplexer_1_out13, demultiplexer_1_out14, demultiplexer_1_out15,
       demultiplexer_1_out16, demultiplexer_1_out17, demultiplexer_1_out18, demultiplexer_1_out19,
       demultiplexer_1_out20, demultiplexer_1_out21, demultiplexer_1_out22, demultiplexer_1_out23,
       demultiplexer_1_out24, demultiplexer_1_out25, demultiplexer_1_out26, demultiplexer_1_out27,
       demultiplexer_1_out28, demultiplexer_1_out29, demultiplexer_1_out30, demultiplexer_1_out31;
  wire [31:0] a0_q, a1_q, a2_q, a3_q, at_q, fp_q, gp_q, k0_q, k1_q, ra_q, s0_q, s1_q, s2_q, s3_q, s4_q, s5_q,
       s6_q, s7_q, sp_q, t0_q, t1_q, t2_q, t3_q, t4_q, t5_q, t6_q, t7_q, t8_q, t9_q, v0_q, v1_q, zero_q;

  Demultiplexer #(.select(5)) demultiplexer_1 (
    .out0(demultiplexer_1_out0), .out1(demultiplexer_1_out1), .out2(demultiplexer_1_out2),
    .out3(demultiplexer_1_out3), .out4(demultiplexer_1_out4), .out5(demultiplexer_1_out5),
    .out6(demultiplexer_1_out6), .out7(demultiplexer_1_out7), .out8(demultiplexer_1_out8),
    .out9(demultiplexer_1_out9), .out10(demultiplexer_1_out10), .out11(demultiplexer_1_out11),
    .out12(demultiplexer_1_out12), .out13(demultiplexer_1_out13), .out14(demultiplexer_1_out14),
    .out15(demultiplexer_1_out15), .out16(demultiplexer_1_out16), .out17(demultiplexer_1_out17),
    .out18(demultiplexer_1_out18), .out19(demultiplexer_1_out19), .out20(demultiplexer_1_out20),
    .out21(demultiplexer_1_out21), .out22(demultiplexer_1_out22), .out23(demultiplexer_1_out23),
    .out24(demultiplexer_1_out24), .out25(demultiplexer_1_out25), .out26(demultiplexer_1_out26),
    .out27(demultiplexer_1_out27), .out28(demultiplexer_1_out28), .out29(demultiplexer_1_out29),
    .out30(demultiplexer_1_out30), .out31(demultiplexer_1_out31), .in(RegWrite), .sel(WriteReg));
  Register #(.width(32)) zero (.D(WriteData), .en(demultiplexer_1_out0), .clk(CLK), .Q(zero_q));  // open: clr
  Register #(.width(32)) a0 (.D(WriteData), .en(demultiplexer_1_out4), .clk(CLK), .Q(a0_q));  // open: clr
  Register #(.width(32)) t0 (.D(WriteData), .en(demultiplexer_1_out8), .clk(CLK), .Q(t0_q));  // open: clr
  Register #(.width(32)) t4 (.D(WriteData), .en(demultiplexer_1_out12), .clk(CLK), .Q(t4_q));  // open: clr
  Register #(.width(32)) s0 (.D(WriteData), .en(demultiplexer_1_out16), .clk(CLK), .Q(s0_q));  // open: clr
  Register #(.width(32)) s4 (.D(WriteData), .en(demultiplexer_1_out20), .clk(CLK), .Q(s4_q));  // open: clr
  Register #(.width(32)) t8 (.D(WriteData), .en(demultiplexer_1_out24), .clk(CLK), .Q(t8_q));  // open: clr
  Register #(.width(32)) gp (.D(WriteData), .en(demultiplexer_1_out28), .clk(CLK), .Q(gp_q));  // open: clr
  Register #(.width(32)) at (.D(WriteData), .en(demultiplexer_1_out1), .clk(CLK), .Q(at_q));  // open: clr
  Register #(.width(32)) a1 (.D(WriteData), .en(demultiplexer_1_out5), .clk(CLK), .Q(a1_q));  // open: clr
  Register #(.width(32)) t1 (.D(WriteData), .en(demultiplexer_1_out9), .clk(CLK), .Q(t1_q));  // open: clr
  Register #(.width(32)) t5 (.D(WriteData), .en(demultiplexer_1_out13), .clk(CLK), .Q(t5_q));  // open: clr
  Register #(.width(32)) s1 (.D(WriteData), .en(demultiplexer_1_out17), .clk(CLK), .Q(s1_q));  // open: clr
  Register #(.width(32)) s5 (.D(WriteData), .en(demultiplexer_1_out21), .clk(CLK), .Q(s5_q));  // open: clr
  Register #(.width(32)) t9 (.D(WriteData), .en(demultiplexer_1_out25), .clk(CLK), .Q(t9_q));  // open: clr
  Register #(.width(32)) sp (.D(WriteData), .en(demultiplexer_1_out29), .clk(CLK), .Q(sp_q));  // open: clr
  Register #(.width(32)) v0 (.D(WriteData), .en(demultiplexer_1_out2), .clk(CLK), .Q(v0_q));  // open: clr
  Register #(.width(32)) a2 (.D(WriteData), .en(demultiplexer_1_out6), .clk(CLK), .Q(a2_q));  // open: clr
  Register #(.width(32)) t2 (.D(WriteData), .en(demultiplexer_1_out10), .clk(CLK), .Q(t2_q));  // open: clr
  Register #(.width(32)) t6 (.D(WriteData), .en(demultiplexer_1_out14), .clk(CLK), .Q(t6_q));  // open: clr
  Register #(.width(32)) s2 (.D(WriteData), .en(demultiplexer_1_out18), .clk(CLK), .Q(s2_q));  // open: clr
  Register #(.width(32)) s6 (.D(WriteData), .en(demultiplexer_1_out22), .clk(CLK), .Q(s6_q));  // open: clr
  Register #(.width(32)) k0 (.D(WriteData), .en(demultiplexer_1_out26), .clk(CLK), .Q(k0_q));  // open: clr
  Register #(.width(32)) fp (.D(WriteData), .en(demultiplexer_1_out30), .clk(CLK), .Q(fp_q));  // open: clr
  Register #(.width(32)) v1 (.D(WriteData), .en(demultiplexer_1_out3), .clk(CLK), .Q(v1_q));  // open: clr
  Register #(.width(32)) a3 (.D(WriteData), .en(demultiplexer_1_out7), .clk(CLK), .Q(a3_q));  // open: clr
  Register #(.width(32)) t3 (.D(WriteData), .en(demultiplexer_1_out11), .clk(CLK), .Q(t3_q));  // open: clr
  Register #(.width(32)) t7 (.D(WriteData), .en(demultiplexer_1_out15), .clk(CLK), .Q(t7_q));  // open: clr
  Register #(.width(32)) s3 (.D(WriteData), .en(demultiplexer_1_out19), .clk(CLK), .Q(s3_q));  // open: clr
  Register #(.width(32)) s7 (.D(WriteData), .en(demultiplexer_1_out23), .clk(CLK), .Q(s7_q));  // open: clr
  Register #(.width(32)) k1 (.D(WriteData), .en(demultiplexer_1_out27), .clk(CLK), .Q(k1_q));  // open: clr
  Register #(.width(32)) ra (.D(WriteData), .en(demultiplexer_1_out31), .clk(CLK), .Q(ra_q));  // open: clr
  Multiplexer #(.select(5), .width(32)) multiplexer_1 (
    .in0(zero_q), .in1(at_q), .in2(v0_q), .in3(v1_q), .in4(a0_q), .in5(a1_q), .in6(a2_q), .in7(a3_q),
    .in8(t0_q), .in9(t1_q), .in10(t2_q), .in11(t3_q), .in12(t4_q), .in13(t5_q), .in14(t6_q), .in15(t7_q),
    .in16(s0_q), .in17(s1_q), .in18(s2_q), .in19(s3_q), .in20(s4_q), .in21(s5_q), .in22(s6_q), .in23(s7_q),
    .in24(t8_q), .in25(t9_q), .in26(k0_q), .in27(k1_q), .in28(gp_q), .in29(sp_q), .in30(fp_q), .in31(ra_q),
    .out(ReadData1), .sel(ReadReg1));
  Multiplexer #(.select(5), .width(32)) multiplexer_2 (
    .in0(zero_q), .in1(at_q), .in2(v0_q), .in3(v1_q), .in4(a0_q), .in5(a1_q), .in6(a2_q), .in7(a3_q),
    .in8(t0_q), .in9(t1_q), .in10(t2_q), .in11(t3_q), .in12(t4_q), .in13(t5_q), .in14(t6_q), .in15(t7_q),
    .in16(s0_q), .in17(s1_q), .in18(s2_q), .in19(s3_q), .in20(s4_q), .in21(s5_q), .in22(s6_q), .in23(s7_q),
    .in24(t8_q), .in25(t9_q), .in26(k0_q), .in27(k1_q), .in28(gp_q), .in29(sp_q), .in30(fp_q), .in31(ra_q),
    .out(ReadData2), .sel(ReadReg2));
endmodule

module Control (
  input  [5:0] Opcode,
  output RegDst,
  output ALUSrc,
  output MemToReg,
  output RegWrite,
  output MemRead,
  output MemWrite,
  output Branch,
  output Jump,
  output [1:0] ALUOp
);

  and Tipo_R (ALUOp[1], ~Opcode[5], ~Opcode[4], ~Opcode[3], ~Opcode[2], ~Opcode[1], ~Opcode[0]);  // AND_Gate
  and lw (MemRead, Opcode[5], ~Opcode[4], ~Opcode[3], ~Opcode[2], Opcode[1], Opcode[0]);  // AND_Gate
  and sw (MemWrite, Opcode[5], ~Opcode[4], Opcode[3], ~Opcode[2], Opcode[1], Opcode[0]);  // AND_Gate
  and beq (ALUOp[0], ~Opcode[5], ~Opcode[4], ~Opcode[3], Opcode[2], ~Opcode[1], ~Opcode[0]);  // AND_Gate
  and j (Jump, ~Opcode[5], ~Opcode[4], ~Opcode[3], ~Opcode[2], Opcode[1], ~Opcode[0]);  // AND_Gate
  or or_1 (ALUSrc, MemRead, MemWrite);
  or or_2 (RegWrite, ALUOp[1], MemRead);

  assign Branch = ALUOp[0];
  assign MemToReg = MemRead;
  assign RegDst = ALUOp[1];
endmodule

module ALU (
  input  [31:0] A,
  input  [31:0] B,
  input  [3:0] ALUControl,
  output Zero,
  output [31:0] Result
);

  wire [31:0] adder_1_out, and_1_out, or_1_out, subtractor_1_out;

  assign and_1_out = A & B;  // AND_Gate and_1, 32 bits wide
  assign or_1_out = A | B;  // OR_Gate or_1, 32 bits wide
  Adder #(.width(32)) adder_1 (.a(A), .b(B), .out(adder_1_out));  // open: cin, cout
  Subtractor #(.width(32)) subtractor_1 (.a(A), .b(B), .out(subtractor_1_out));  // open: bin, bout
  Multiplexer #(.select(4), .width(32)) multiplexer_1 (
    .in0(and_1_out), .in1(or_1_out), .in2(adder_1_out), .in6(subtractor_1_out), .out(Result), .sel(ALUControl));  // open: in3, in4, in5, in7, in8, in9, in10, in11, in12, in13, in14, in15
  and and_2 (Zero, ~Result[0], ~Result[1], ~Result[2], ~Result[3], ~Result[4], ~Result[5], ~Result[6], ~Result[7], ~Result[8], ~Result[9], ~Result[10], ~Result[11], ~Result[12], ~Result[13], ~Result[14], ~Result[15], ~Result[16], ~Result[17], ~Result[18], ~Result[19], ~Result[20], ~Result[21], ~Result[22], ~Result[23], ~Result[24], ~Result[25], ~Result[26], ~Result[27], ~Result[28], ~Result[29], ~Result[30], ~Result[31]);  // AND_Gate
endmodule

module ALUControl (
  input  [1:0] ALUOp,
  input  [5:0] Funct,
  output [3:0] ALU_Control
);

  wire and_1_out;

  and and_1 (and_1_out, Funct[1], ALUOp[1]);
  or or_1 (ALU_Control[1], ~Funct[2], ~ALUOp[1]);  // OR_Gate
  and and_2 (ALU_Control[0], Funct[2], Funct[0], ALUOp[1]);
  or or_2 (ALU_Control[2], ALUOp[0], and_1_out);

  assign ALU_Control[3] = 1'b0;
endmodule

module DataMemory (
  input  [31:0] Address,
  input  CLK,
  input  [31:0] WriteData,
  input  MemWrite,
  input  MemRead,
  output [31:0] ReadData
);

  RAM #(.addrWidth(24), .asyncread("true"), .dataWidth(32)) ram_1 (
    .addr(Address[23:0]), .we(MemWrite), .oe(MemRead), .clk(CLK), .din(WriteData), .dout(ReadData));
endmodule
